# Fritzing sketch ESP8266_InfraredRemoteControl (saved by Fritzing 0.9.4)
breadboards: 1

parts:
  U1 = NodeMCU V1.0
  IR_Receiver1 = IR_Receiver

nets:
  N1: U1.D1, IR_Receiver1.OUT
  3V3: U1.3V3, IR_Receiver1.VCC
  GND: U1.GND, IR_Receiver1.GND

custom parts:
  NodeMCU V1.0: ESP8266 based NodeMCU
  IR_Receiver: 赤外線受信モジュール GP1UXC41QS
